# Fritzing sketch arduino_mega (saved by Fritzing 0.9.3b)
breadboards: 1

parts:
  Part1 = Arduino Mega 2560 (Rev3)
  LCD1 = LCD screen
  R1 = Trimmer Potentiometer [maximum_resistance=10kΩ package=THT]
  R2 = Resistor [tolerance=±5% resistance=220 package="2512 [SMD]"]
  J1 = Basic Servo
  J2 = Infrared Proximity Sensor
  Matrix_keypad2 = KEYPAD 4x4
  RC522 = RFID USB Reader
  J3 = Piezo Speaker

nets:
  N1: Part1.GND, RC522.GNDT
  N2: Part1.D12_PWM, LCD1.RS
  N3: Part1.D10_PWM, J1.pulse
  VCC: Part1.5V, LCD1.VDD, R1.leg1, R2.Pin_1, J1.vcc, J2.Vcc, RC522.CP
  N4: Part1.D6_PWM, J2.Vout
  N5: Part1.D22, Matrix_keypad2.col1
  N6: Part1.D24, Matrix_keypad2.col2
  N7: Part1.D26, Matrix_keypad2.col3
  N8: Part1.D28, Matrix_keypad2.col4
  N9: Part1.D30, Matrix_keypad2.row1
  N10: Part1.D32, Matrix_keypad2.row2
  N11: Part1.D34, Matrix_keypad2.row3
  N12: Part1.D36, Matrix_keypad2.row4
  N13: Part1.D38, J3.pin2
  N14: Part1.D50, RC522.ANT2
  N15: Part1.D51, RC522.ANT1
  N16: Part1.D52, RC522.TX-O-RS232
  GND: LCD1.VSS, LCD1.R/W, LCD1.LED-, R1.leg2, J1.gnd, J2.GND, J3.pin1
  N17: LCD1.V0, R1.wiper
  N18: LCD1.LED+, R2.Pin_0

custom parts:
  KEYPAD 4x4: Matrix keypad 16 buttons, 4 rows x 4 columns
