# Fritzing sketch arduino_yun_xPNOvwVdbH (saved by Fritzing 0.9.3b)
breadboards: 1

parts:
  DHT_11 = Humidity and Temperature Sensor RHT03
  RHT2 = Humidity and Temperature Sensor RHT03
  Flame_Sensor = Infrared Proximity Sensor
  Part1 = Arduino Yun
  DC_Motor_Fan = Basic Servo
  Geysar_Led_(_3_3_V_) = LED - 5mm [color="Red (633nm)" package="5 mm [THT]"]
  Washing_Machine_LED_(3_3_V) = LED - 5mm [color="Red (633nm)" package="5 mm [THT]"]
  Lights_LED = LED - 5mm [color="Red (633nm)" package="5 mm [THT]"]

nets:
  VCC: DHT_11.GND_1, RHT2.GND_1, Flame_Sensor.Vcc, Part1.5V, DC_Motor_Fan.vcc
  GND: DHT_11.GND_2, RHT2.GND_2, Flame_Sensor.GND, Part1.GND, DC_Motor_Fan.gnd, Geysar_Led_(_3_3_V_).cathode, Washing_Machine_LED_(3_3_V).cathode, Lights_LED.cathode
  N1: Flame_Sensor.Vout, Part1.A0
  N2: Part1.D9_PWM, DC_Motor_Fan.pulse
  N3: Part1.D11_PWM/MOSI, Geysar_Led_(_3_3_V_).anode
  N4: Part1.D6_PWM, Lights_LED.anode
  N5: Part1.D7, Washing_Machine_LED_(3_3_V).anode
